// Logisim project control-logic.circ as structural Verilog: 1 circuit, main circuit control_logic
module control_logic (
  input  [31:0] Instruction,
  input  BrEq,
  input  BrLt,
  output PCSel,
  output RegWEn,
  output [2:0] ImmSel,
  output BrUn,
  output ASel,
  output BSel,
  output [3:0] ALUSel,
  output MemWEn,
  output [1:0] WBSel
);

  wire [5:0] undriven;
  wire [6:0] multiplexer_1_out;
  wire [15:14] rom_1_data;

  Multiplexer #(.select(3), .width(7)) multiplexer_1 (
    .in0(7'b0110011), .in1(7'b0000011), .in2(7'b0010011), .in3(7'b0100011), .in4(7'b1100011),
    .in5(7'b0010111), .in6(7'b0110111), .out(multiplexer_1_out), .sel(Instruction[31:29]));  // open: in7
  Priority_Encoder priority_encoder_1 ();  // open: in0, in1, in2, in3, in4, in5, in6, in7, out, en_in, gs, en_out
  ROM #(.addrWidth(6), .dataWidth(16)) rom_1 (
    .addr(undriven), .data({rom_1_data, WBSel, MemWEn, ALUSel, BSel, ASel, BrUn, ImmSel, RegWEn}));

  // Notes on the sheet:
  //   INPUTS to your circuit
  //   DON'T CHANGE THE LOCATIONS OF THE INPUTS AND OUTPUTS!
  //   OUTPUT from your circuit
  //   Connect ROM Input here ->
  //   contents of rom_1 (hex, n*v repeats v):
  //   1001 1401 1601 1081 1481 1581 1101 1201 1281 1681 1301 1381 4*1041 10c1 1141 1241 12c1 16c1 1341
  //   13c1 842 842 842 4*1064 1074 1074 1067 1047 1069 1041
  //   ROM FOR CONTROL LOGIC
  //   This is only if you choose to do the ROM option
  //   WIRE
  //   CONNECT
  //   USE
  //   ROM
  //   Reminder: If using ROM, use combinational logic for PCSel
endmodule
