// Logisim project imm-gen.circ as structural Verilog: 1 circuit, main circuit imm_gen
module imm_gen (
  input  [31:0] Instruction,
  input  [2:0] ImmSel,
  output [31:0] Immediate
);

  wire multiplexer_1_out;
  wire [31:0] bit_extender_2_out, bit_extender_3_out, bit_extender_4_out, bit_extender_5_out,
       bit_extender_6_out;

  assign Immediate = {{12{Instruction[31]}}, Instruction[31:12]};  // Bit_Extender bit_extender_1
  assign bit_extender_2_out = {{20{Instruction[31]}}, Instruction[31:20]};  // Bit_Extender bit_extender_2
  assign bit_extender_3_out = {{27{Instruction[24]}}, Instruction[24:20]};  // Bit_Extender bit_extender_3
  assign bit_extender_4_out = {{20{Instruction[31]}}, {Instruction[31:25], Instruction[11:7]}};  // Bit_Extender bit_extender_4
  assign bit_extender_5_out = {{20{Instruction[31]}}, {Instruction[31], Instruction[7], Instruction[30:25], Instruction[11:8]}};  // Bit_Extender bit_extender_5
  assign bit_extender_6_out = {{12{Instruction[31]}}, {Instruction[31], Instruction[21:12], Instruction[22], Instruction[30:23]}};  // Bit_Extender bit_extender_6
  Multiplexer multiplexer_1 (.out(multiplexer_1_out));  // open: in0, in1, sel

  // Notes on the sheet:
  //   INPUTS to your circuit
  //   DON'T CHANGE THE LOCATIONS OF THE INPUTS AND OUTPUTS!
  //   OUTPUT from your circuit
endmodule
